# Fritzing sketch Circuit_1_Blink (saved by Fritzing 0.9.1b)
breadboards: 1

parts:
  RedBoard1 = RedBoard [part_number=DEV-11575]
  R1 = Resistor [tolerance=±5% resistance=330 package=THT]
  LED1 = LED - 5mm [color="Red (633nm)" package="5 mm [THT]"]

nets:
  N1: RedBoard1.GND, LED1.cathode
  N2: RedBoard1.D13, R1.Pin_1
  N3: R1.Pin_0, LED1.anode

custom parts:
  RedBoard: At SparkFun we use many Arduinos and we're always looking for the simplest, most stable one. Each board is a bit different and no one board has everything we want, so we decided to make our own version that combines all our favorite features. The RedBoard combines the simplicity of the UNO's Optiboot bootloader (which is used in the Pro series), the stability of the FTDI (which we all missed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

// code stored in the sketch: Blink.ino

//setup runs once at the begining of your sketch
void setup()
{
pinMode(13,OUTPUT);	//set pin 13 as an output
}

//loop runs over and over again until you turn the power off!
void loop()
{
//Turn 13 on or "HIGH"
digitalWrite(13,HIGH);	
//wait 1 second (1000 millis)
delay(1000);	
//Turn 13 off or "LOW"
digitalWrite(13,LOW);	
//wait 1 second
delay(1000);	
}
