# Fritzing sketch Circuit_5A_Switch_MultiBlink (saved by Fritzing 0.9.1b)
breadboards: 1

parts:
  RedBoard1 = RedBoard [part_number=DEV-11575]
  S1 = Toggle Switch [package=THT]
  LED1 = LED - 5mm [color="Red (633nm)" package="5 mm [THT]"]
  LED2 = LED - 5mm [color="Red (633nm)" package="5 mm [THT]"]
  LED3 = LED - 5mm [color="Red (633nm)" package="5 mm [THT]"]
  LED4 = LED - 5mm [color="Red (633nm)" package="5 mm [THT]"]
  R1 = Resistor [tolerance=±5% resistance=330 package=THT]
  R2 = Resistor [tolerance=±5% resistance=330 package=THT]
  R3 = Resistor [tolerance=±5% resistance=330 package=THT]
  R4 = Resistor [tolerance=±5% resistance=330 package=THT]
  R5 = Resistor [tolerance=±5% resistance=10k package=THT]

nets:
  N1: RedBoard1.D8, R1.Pin_0
  N2: RedBoard1.D7, R2.Pin_0
  N3: RedBoard1.D6, R3.Pin_0
  N4: RedBoard1.D5, R4.Pin_0
  N5: RedBoard1.D2, S1.COM, R5.Pin_0
  N6: RedBoard1.+5V, S1.L2
  N7: RedBoard1.GND, S1.L1, LED1.cathode, LED2.cathode, LED3.cathode, LED4.cathode, R5.Pin_1
  N8: LED1.anode, R2.Pin_1
  N9: LED2.anode, R3.Pin_1
  N10: LED3.anode, R4.Pin_1
  N11: LED4.anode, R1.Pin_1

custom parts:
  RedBoard: At SparkFun we use many Arduinos and we're always looking for the simplest, most stable one. Each board is a bit different and no one board has everything we want, so we decided to make our own version that combines all our favorite features. The RedBoard combines the simplicity of the UNO's Optiboot bootloader (which is used in the Pro series), the stability of the FTDI (which we all missed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

// code stored in the sketch: Switch_Cylon.ino
void setup()
{
//pins 13 through 8 as outputs
 pinMode(8, OUTPUT);
 pinMode(7, OUTPUT);
 pinMode(6, OUTPUT);
 pinMode(5, OUTPUT);
 pinMode(4, OUTPUT);
 pinMode(3, OUTPUT);
//pin 2 set as input (button)
 pinMode(2,INPUT);
}

void loop()
{
 boolean buttonState = digitalRead(2);
 
 if(buttonState == 1)
  {

   for(int i= 8; i>=4; i--)
   {
    digitalWrite(i,HIGH);
    delay(500);
    digitalWrite(i,LOW);
    delay(500);
   }
}
 else
 {
    for(int i= 8; i>=4; i--)
   {
    digitalWrite(i,HIGH);
    delay(100);
    digitalWrite(i,LOW);
    delay(100);
   }
 }
}
