# Fritzing sketch Circuit_5B_Button_MultiBlink (saved by Fritzing 0.9.1b)
breadboards: 1

parts:
  RedBoard1 = RedBoard [part_number=DEV-11575]
  S1 = Pushbutton [package="[THT]"]
  R5 = Resistor [tolerance=±5% resistance=10k package=THT]
  LED1 = LED - 5mm [color="Red (633nm)" package="5 mm [THT]"]
  LED2 = LED - 5mm [color="Red (633nm)" package="5 mm [THT]"]
  LED4 = LED - 5mm [color="Red (633nm)" package="5 mm [THT]"]
  LED3 = LED - 5mm [color="Red (633nm)" package="5 mm [THT]"]
  R1 = Resistor [tolerance=±5% resistance=330 package=THT]
  R3 = Resistor [tolerance=±5% resistance=330 package=THT]
  R4 = Resistor [tolerance=±5% resistance=330 package=THT]
  R2 = Resistor [tolerance=±5% resistance=330 package=THT]

nets:
  N1: RedBoard1.GND, R5.Pin_0, LED1.cathode, LED2.cathode, LED4.cathode, LED3.cathode
  N2: RedBoard1.D7, R1.Pin_0
  N3: RedBoard1.D6, R2.Pin_0
  N4: RedBoard1.D5, R3.Pin_0
  N5: RedBoard1.D4, R4.Pin_0
  N6: RedBoard1.D2, S1.Pin_3, S1.Pin_4, R5.Pin_1
  N7: RedBoard1.+5V, S1.Pin_1, S1.Pin_2
  N8: LED1.anode, R1.Pin_1
  N9: LED2.anode, R2.Pin_1
  N10: LED4.anode, R4.Pin_1
  N11: LED3.anode, R3.Pin_1

custom parts:
  RedBoard: At SparkFun we use many Arduinos and we're always looking for the simplest, most stable one. Each board is a bit different and no one board has everything we want, so we decided to make our own version that combines all our favorite features. The RedBoard combines the simplicity of the UNO's Optiboot bootloader (which is used in the Pro series), the stability of the FTDI (which we all missed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
