# Fritzing sketch Circuit_4_Button_LED (saved by Fritzing 0.9.1b)
breadboards: 1

parts:
  RedBoard1 = RedBoard [part_number=DEV-11575]
  S1 = Pushbutton [package="[THT]"]
  R5 = Resistor [tolerance=±5% resistance=10k package=THT]
  LED1 = LED - 5mm [color="Red (633nm)" package="5 mm [THT]"]
  R6 = Resistor [tolerance=±5% resistance=330 package=THT]

nets:
  N1: RedBoard1.D13, R6.Pin_0
  N2: RedBoard1.D12, S1.Pin_3, S1.Pin_4, R5.Pin_1
  N3: RedBoard1.+5V, S1.Pin_1, S1.Pin_2
  N4: RedBoard1.GND, R5.Pin_0, LED1.cathode
  N5: LED1.anode, R6.Pin_1

custom parts:
  RedBoard: At SparkFun we use many Arduinos and we're always looking for the simplest, most stable one. Each board is a bit different and no one board has everything we want, so we decided to make our own version that combines all our favorite features. The RedBoard combines the simplicity of the UNO's Optiboot bootloader (which is used in the Pro series), the stability of the FTDI (which we all missed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

// code stored in the sketch: Button_Serial.ino
void setup()
{
 //set pin 13 as output (LED)
 pinMode(13,OUTPUT);
 //set pin 12 as an input (Button)
 pinMode(12,INPUT);
 //Start serial communication at 9600 bits per second
 Serial.begin(9600);
}

void loop()
{
 //create a boolean variable called buttonState and assign it to the input of pin 9
 boolean buttonState = digitalRead(12);
 //write buttonState to pin 13 to control LED on pin 13
 digitalWrite(13, buttonState);
 //print buttonState and millis to the Serial Monitor
 Serial.print(buttonState);
 Serial.print(" , ");
 //use println to end with a carriage return
 Serial.println(millis());
 //wait 10 ms for debounce
 delay(10); 
}
