# Fritzing sketch Circuit_18_Sensor_Buzzer (saved by Fritzing 0.9.1b)
breadboards: 1

parts:
  RedBoard1 = RedBoard [part_number=DEV-11575]
  J1 = Piezo Speaker
  Part1 = Triple Axis Accelerometer Breakout - ADXL335

nets:
  GND: RedBoard1.GND, J1.pin1, Part1.GND
  N1: RedBoard1.D11, J1.pin2
  3V3: RedBoard1.3V3, Part1.VCC
  N2: RedBoard1.A0, Part1.ZOUT
  N3: RedBoard1.A1, Part1.YOUT
  N4: RedBoard1.A2, Part1.XOUT

custom parts:
  RedBoard: At SparkFun we use many Arduinos and we're always looking for the simplest, most stable one. Each board is a bit different and no one board has everything we want, so we decided to make our own version that combines all our favorite features. The RedBoard combines the simplicity of the UNO's Optiboot bootloader (which is used in the Pro series), the stability of the FTDI (which we all missed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
