# Fritzing sketch Circuit_8_RGB_ColorMixer (saved by Fritzing 0.9.1b)
breadboards: 1

parts:
  RedBoard1 = RedBoard [part_number=DEV-11575]
  R5 = Trimmer Potentiometer [maximum_resistance=10kΩ package=THT]
  LED1 = RGB LED (com. cathode, rgb) [package="5 mm [THT]"]
  R6 = Resistor [tolerance=±5% resistance=330 package=THT]
  R7 = Resistor [tolerance=±5% resistance=330 package=THT]
  R8 = Resistor [tolerance=±5% resistance=330 package=THT]
  R9 = Trimmer Potentiometer [maximum_resistance=10kΩ package=THT]
  R10 = Trimmer Potentiometer [maximum_resistance=10kΩ package=THT]

nets:
  N1: RedBoard1.D11, R8.Pin_0
  N2: RedBoard1.D10, R7.Pin_0
  N3: RedBoard1.D9, R6.Pin_0
  N4: RedBoard1.+5V, R5.leg2, R9.leg2, R10.leg2
  N5: RedBoard1.A0, R5.wiper
  N6: RedBoard1.A1, R9.wiper
  N7: RedBoard1.A2, R10.wiper
  N8: R5.leg1, LED1.common_cathode, R9.leg1, R10.leg1
  N9: LED1.red_anode, R6.Pin_1
  N10: LED1.green_anode, R7.Pin_1
  N11: LED1.blue_anode, R8.Pin_1

custom parts:
  RedBoard: At SparkFun we use many Arduinos and we're always looking for the simplest, most stable one. Each board is a bit different and no one board has everything we want, so we decided to make our own version that combines all our favorite features. The RedBoard combines the simplicity of the UNO's Optiboot bootloader (which is used in the Pro series), the stability of the FTDI (which we all missed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

// code stored in the sketch: color_mixer.ino
void setup()
{
  pinMode(9,OUTPUT);
  pinMode(10,OUTPUT);
  pinMode(11,OUTPUT);
}

void loop()
{
int r= analogRead(A0); 
int g= analogRead(A1);
int b= analogRead(A2);

analogWrite(9,r/4);
analogWrite(10,g/4);
analogWrite(11,b/4);
}
