# Fritzing sketch Circuit_7_Dimmer (saved by Fritzing 0.9.1b)
breadboards: 1

parts:
  RedBoard1 = RedBoard [part_number=DEV-11575]
  LED4 = LED - 5mm [color="Red (633nm)" package="5 mm [THT]"]
  R4 = Resistor [tolerance=±5% resistance=330 package=THT]
  R5 = Trimmer Potentiometer [maximum_resistance=10kΩ package=THT]

nets:
  N1: RedBoard1.GND, LED4.cathode, R5.leg1
  N2: RedBoard1.D9, R4.Pin_0
  N3: RedBoard1.+5V, R5.leg2
  N4: RedBoard1.A3, R5.wiper
  N5: LED4.anode, R4.Pin_1

custom parts:
  RedBoard: At SparkFun we use many Arduinos and we're always looking for the simplest, most stable one. Each board is a bit different and no one board has everything we want, so we decided to make our own version that combines all our favorite features. The RedBoard combines the simplicity of the UNO's Optiboot bootloader (which is used in the Pro series), the stability of the FTDI (which we all missed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

// code stored in the sketch: Dimmer.ino
void setup()
{
  Serial.begin(9600);
}

void loop()
{
  int val = analogRead(A3);
  
  Serial.println(val);
  analogWrite(9,val/4);
  delay(10);
}
