# Fritzing sketch Circuit_6_Fade (saved by Fritzing 0.9.1b)
breadboards: 1

parts:
  RedBoard1 = RedBoard [part_number=DEV-11575]
  LED4 = LED - 5mm [color="Red (633nm)" package="5 mm [THT]"]
  R4 = Resistor [tolerance=±5% resistance=330 package=THT]

nets:
  N1: RedBoard1.GND, LED4.cathode
  N2: RedBoard1.D9, R4.Pin_0
  N3: LED4.anode, R4.Pin_1

custom parts:
  RedBoard: At SparkFun we use many Arduinos and we're always looking for the simplest, most stable one. Each board is a bit different and no one board has everything we want, so we decided to make our own version that combines all our favorite features. The RedBoard combines the simplicity of the UNO's Optiboot bootloader (which is used in the Pro series), the stability of the FTDI (which we all missed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

// code stored in the sketch: Fade.ino
int val = 0;
int grow = 5;


void setup()
{
  pinMode(9,OUTPUT);
}

void loop()
{
//with a for loop
for(int i= 0; i<=255; i++)
{
  analogWrite(9,i);
  delay(10);
}
for(int i= 255; i>=0; i--);
{
  analogWrite(9,i);
  delay(10);
}

//with a variable and an if() statement
/*

val = val+grow;

if(val<=0||val>=255)
{
  grow = grow*-1;
}
analogWrite(9,val);
delay(10);

*/
}
