# Fritzing sketch Circuit_14_H_Bridge (saved by Fritzing 0.9.1b)
breadboards: 1

parts:
  RedBoard1 = RedBoard [part_number=DEV-11575]
  IC1 = H-Bridge [package=THT]
  M1 = DC Motor

nets:
  GND: RedBoard1.GND, IC1.GND1
  N1: RedBoard1.D13, IC1.1A
  N2: RedBoard1.D12, IC1.2A
  N3: RedBoard1.D11, IC1.1_2EN
  N4: RedBoard1.+5V, IC1.VCC2, IC1.VCC1
  N5: IC1.1Y, M1.pin_1
  N6: IC1.2Y, M1.pin_2

custom parts:
  RedBoard: At SparkFun we use many Arduinos and we're always looking for the simplest, most stable one. Each board is a bit different and no one board has everything we want, so we decided to make our own version that combines all our favorite features. The RedBoard combines the simplicity of the UNO's Optiboot bootloader (which is used in the Pro series), the stability of the FTDI (which we all missed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
