# Fritzing sketch Circuit_15_IR_Pair_Serial_LCD (saved by Fritzing 0.9.1b)
breadboards: 1

parts:
  RedBoard1 = RedBoard [part_number=DEV-11575]
  R1 = Resistor [tolerance=±5% resistance=330 package=THT]
  U1 = LCD-16X2 [package=lcd-16x2]
  Q1 = LTR-301 [package=ltr-301]
  Q2 = LTR-301 [package=ltr-301]

nets:
  N1: RedBoard1.D13, R1.Pin_0
  N2: RedBoard1.D4, Q2.E
  N3: RedBoard1.D2, U1.VO
  +5V: RedBoard1.+5V, U1.VDD
  GND: RedBoard1.GND, U1.VSS, Q1.C, Q2.C
  N4: R1.Pin_1, Q1.E

custom parts:
  RedBoard: At SparkFun we use many Arduinos and we're always looking for the simplest, most stable one. Each board is a bit different and no one board has everything we want, so we decided to make our own version that combines all our favorite features. The RedBoard combines the simplicity of the UNO's Optiboot bootloader (which is used in the Pro series), the stability of the FTDI (which we all missed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
