# Fritzing sketch Circuit_9_NightLight (saved by Fritzing 0.9.1b)
breadboards: 1

parts:
  RedBoard1 = RedBoard [part_number=DEV-11575]
  LED1 = LED - 5mm [color="Red (633nm)" package="5 mm [THT]"]
  R1 = Resistor [tolerance=±5% resistance=330 package=THT]
  R2 = Photocell (LDR) [package=THT]
  R3 = Resistor [tolerance=±5% resistance=10k package=THT]

nets:
  N1: RedBoard1.D9, R1.Pin_0
  N2: RedBoard1.+5V, R2.pin_1
  N3: RedBoard1.GND, LED1.cathode, R3.Pin_0
  N4: RedBoard1.A1, R2.pin_0, R3.Pin_1
  N5: LED1.anode, R1.Pin_1

custom parts:
  RedBoard: At SparkFun we use many Arduinos and we're always looking for the simplest, most stable one. Each board is a bit different and no one board has everything we want, so we decided to make our own version that combines all our favorite features. The RedBoard combines the simplicity of the UNO's Optiboot bootloader (which is used in the Pro series), the stability of the FTDI (which we all missed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

// code stored in the sketch: Night_Light.ino
int inittVal;

void setup()
{
 pinMode(9,OUTPUT);
 setVal = analogRead(A1);
 Serial.begin(9600);
}

void loop()
{
 int currentVal = analogRead(A1); 

 if(currentVal < initVal -10 )
 {
  digitalWrite(9,HIGH);
 }
 
else
 {
 digitalWrite(9,LOW);
 }
}
