# Fritzing sketch Circuit_2_RR_Crossing (saved by Fritzing 0.9.1b)
breadboards: 1

parts:
  RedBoard1 = RedBoard [part_number=DEV-11575]
  R1 = Resistor [tolerance=±5% resistance=330 package=THT]
  LED1 = LED - 5mm [color="Red (633nm)" package="5 mm [THT]"]
  LED2 = LED - 5mm [color="Red (633nm)" package="5 mm [THT]"]
  R2 = Resistor [tolerance=±5% resistance=330 package=THT]

nets:
  N1: RedBoard1.GND, LED1.cathode, LED2.cathode
  N2: RedBoard1.D13, R1.Pin_1
  N3: RedBoard1.D12, R2.Pin_1
  N4: R1.Pin_0, LED1.anode
  N5: LED2.anode, R2.Pin_0

custom parts:
  RedBoard: At SparkFun we use many Arduinos and we're always looking for the simplest, most stable one. Each board is a bit different and no one board has everything we want, so we decided to make our own version that combines all our favorite features. The RedBoard combines the simplicity of the UNO's Optiboot bootloader (which is used in the Pro series), the stability of the FTDI (which we all missed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

// code stored in the sketch: RR_Crossing.ino
void setup()
{
//pins 13 and 12 as outputs
pinMode(13,OUTPUT);
pinMode(12,OUTPUT);
}

void loop()
{
//pin 13 on and 12 off
digitalWrite(13,HIGH);
digitalWrite(12,LOW);
//wait 500 ms
delay(500);
//pin 13 off and 12 on
digitalWrite(13,LOW);
digitalWrite(12,HIGH);
//wait 500ms
delay(500);
}
