# Fritzing sketch Circuit_13_Therm_Serial_LCD (saved by Fritzing 0.9.1b)
breadboards: 1

parts:
  RedBoard1 = RedBoard [part_number=DEV-11575]
  R2 = Temperature Sensor (Thermistor) [thermistor_type=NTC package=THT]
  R3 = Resistor [tolerance=±5% resistance=10k package=THT]
  U1 = LCD-16X2 [package=lcd-16x2_noholes]

nets:
  GND: RedBoard1.GND, R3.Pin_1, U1.VSS
  N1: RedBoard1.D1TX, U1.VO
  +5V: RedBoard1.+5V, R2.pin_0, U1.VDD
  N2: RedBoard1.A0, R2.pin_1, R3.Pin_0

notes:
  Serial LCD!

custom parts:
  RedBoard: At SparkFun we use many Arduinos and we're always looking for the simplest, most stable one. Each board is a bit different and no one board has everything we want, so we decided to make our own version that combines all our favorite features. The RedBoard combines the simplicity of the UNO's Optiboot bootloader (which is used in the Pro series), the stability of the FTDI (which we all missed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
