# Fritzing sketch Circuit_10_Servo_Knob (saved by Fritzing 0.9.1b)
breadboards: 1

parts:
  RedBoard1 = RedBoard [part_number=DEV-11575]
  R2 = Trimmer Potentiometer [maximum_resistance=10kΩ package=THT]
  J1 = Basic Servo

nets:
  N1: RedBoard1.D3, J1.pulse
  +5V: RedBoard1.+5V, R2.leg2, J1.vcc
  GND: RedBoard1.GND, R2.leg1, J1.gnd
  N2: RedBoard1.A3, R2.wiper

custom parts:
  RedBoard: At SparkFun we use many Arduinos and we're always looking for the simplest, most stable one. Each board is a bit different and no one board has everything we want, so we decided to make our own version that combines all our favorite features. The RedBoard combines the simplicity of the UNO's Optiboot bootloader (which is used in the Pro series), the stability of the FTDI (which we all missed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

// code stored in the sketch: Servo_Knob.ino
#include <Servo.h>

Servo myServo;

void setup()
{
  myServo.attach(3);
}

void loop()
{
  int val = analogRead(A3);
  val = map(val,0,1023,0,180);

  myServo.Write(val);
  delay(10);
}
