# Fritzing sketch Circuit_17_SoundDetector_BarGraph (saved by Fritzing 0.9.1b)
breadboards: 1

parts:
  RedBoard1 = RedBoard [part_number=DEV-11575]
  LED1 = LED - 5mm [color="Red (633nm)" package="5 mm [THT]"]
  LED2 = LED - 5mm [color="Red (633nm)" package="5 mm [THT]"]
  LED3 = LED - 5mm [color="Red (633nm)" package="5 mm [THT]"]
  LED4 = LED - 5mm [color="Red (633nm)" package="5 mm [THT]"]
  R1 = Resistor [tolerance=±5% resistance=330 package=THT]
  R2 = Resistor [tolerance=±5% resistance=330 package=THT]
  R3 = Resistor [tolerance=±5% resistance=330 package=THT]
  R4 = Resistor [tolerance=±5% resistance=330 package=THT]
  PART1 = Sound Detector  # not connected

nets:
  N1: RedBoard1.GND, LED1.cathode, LED2.cathode, LED3.cathode, LED4.cathode
  N2: RedBoard1.D13, R1.Pin_0
  N3: RedBoard1.D12, R2.Pin_0
  N4: RedBoard1.D11, R3.Pin_0
  N5: RedBoard1.D10, R4.Pin_0
  N6: LED1.anode, R1.Pin_1
  N7: LED2.anode, R4.Pin_1
  N8: LED3.anode, R2.Pin_1
  N9: LED4.anode, R3.Pin_1

custom parts:
  RedBoard: At SparkFun we use many Arduinos and we're always looking for the simplest, most stable one. Each board is a bit different and no one board has everything we want, so we decided to make our own version that combines all our favorite features. The RedBoard combines the simplicity of the UNO's Optiboot bootloader (which is used in the Pro series), the stability of the FTDI (which we all missed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
  Sound Detector: Electret microphone with multiple outputs. - First output is the actual audio - Second output is the amplitude envelope - Third output is a binary "sound present" indication - high while sound is present, low otherwise. Visit sparkfun.com for more documentations.
