# Fritzing sketch Circuit_12_Thermistor_Motor (saved by Fritzing 0.9.1b)
breadboards: 1

parts:
  RedBoard1 = RedBoard [part_number=DEV-11575]
  Q1 = NPN-Transistor [package="TO92 [THT]"]
  R1 = Resistor [tolerance=±5% resistance=330 package=THT]
  M1 = DC Motor
  D1 = Zener Diode [part_number=1N4732A breakdown_voltage=3.6V package="300 mil [THT]"]
  R2 = Temperature Sensor (Thermistor) [thermistor_type=NTC package=THT]
  R3 = Resistor [tolerance=±5% resistance=10k package=THT]

nets:
  N1: RedBoard1.GND, Q1.C, R3.Pin_1
  N2: RedBoard1.D9, R1.Pin_1
  N3: RedBoard1.+5V, M1.pin_2, D1.cathode, R2.pin_0
  N4: RedBoard1.A0, R2.pin_1, R3.Pin_0
  N5: Q1.E, M1.pin_1, D1.anode
  N6: Q1.B, R1.Pin_0

custom parts:
  RedBoard: At SparkFun we use many Arduinos and we're always looking for the simplest, most stable one. Each board is a bit different and no one board has everything we want, so we decided to make our own version that combines all our favorite features. The RedBoard combines the simplicity of the UNO's Optiboot bootloader (which is used in the Pro series), the stability of the FTDI (which we all missed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
